# Fritzing sketch AulaUltrassomico (saved by Fritzing 0.9.3b)
breadboards: 1

parts:
  hc-sr1 = hc-sr04
  Componente1 = Arduino Uno (Rev3)
  LED1 = LED - 5mm [color="Red (633nm)" package="5 mm [THT]"]
  R1 = Resistor [tolerance=±5% resistance=220 package=THT]

nets:
  VCC: hc-sr1.VCC, Componente1.5V
  N1: hc-sr1.Trig, Componente1.D12/MISO
  N2: hc-sr1.Echo, Componente1.D13/SCK
  GND: hc-sr1.GND, Componente1.GND, R1.Pin_1
  N3: Componente1.D2, LED1.anode
  N4: LED1.cathode, R1.Pin_0
